// Digital circuit CPU 4.dig as structural Verilog
module CPU_4 (
  input  Clock,
  output CLK1,
  output CLK2
);

  wire _74245_1_p13, _74245_1_p14, _74245_1_p15, _74245_1_p16, _74245_1_p17, _74245_1_p18, _74245_1_p19,
       _74245_1_p20, and_1_out, and_2_out, and_7_out, bussplitter_1_d0, bussplitter_1_d1, bussplitter_1_d2,
       bussplitter_1_d3, bussplitter_1_d4, bussplitter_1_d5, bussplitter_1_d6, bussplitter_1_d7, C_SEL,
       C_VAL, CARRY, demultiplexer_2_out_1, demultiplexer_2_out_2, demultiplexer_2_out_3,
       demultiplexer_2_out_4, demultiplexer_3_out_1, demultiplexer_3_out_2, demultiplexer_3_out_3,
       demultiplexer_4_out_1, demultiplexer_4_out_2, demultiplexer_4_out_3, demultiplexer_4_out_4,
       demultiplexer_4_out_7, JMP_C, JMP_EN, JMP_POS, JMP_Z, JS, multiplexer_2_out, nA_DOUT, nA_ST,
       nand_1_out, nDISP_ST, nMAR_ST, nMEM_DOUT, nMEM_ST, not_1_out, not_6_out, not_8_out, not_9_out,
       not_15_out, not_16_out, not_17_out, not_18_out, nPC_ST, nROM_DOUT, nSUM_DOUT, nSUM_ST, or_2_out,
       or_3_out, t_ff_1_nq, t_ff_1_q, ZERO;
  wire [1:0] and_8_out, ISEL, JMP_SEL, nor_1_out, nor_2_out;
  wire [2:0] DOUT, ST;
  wire [2:2] demultiplexer_5_out_1;
  wire [3:0] H_d, H_d_2, O_d, T_d, T_d_2;
  wire [7:0] A_q, add_1_s, bitextender_1_out, DATA, dipswitch_8_out, DISP_q, MAR_q, MEM__64x8_d, PC_out,
       SUM_q, xor_1_out;
  wire [7:4] O_d_2;
  wire [13:0] IWORD;
  wire [15:0] rom_1_d;

  LED SL1 (.in(ISEL[1]));
  LED SL0 (.in(ISEL[0]));
  LED ST2 (.in(IWORD[13]));
  CounterPreset #(.Bits(8)) PC (
    .en(~1'b0), .C(CLK2), .dir(1'b0), .in(DATA), .ld(~nPC_ST), .clr(1'b0), .out(PC_out));  // open: ovf
  Demultiplexer #(.Selector_Bits(2)) demultiplexer_1 (
    .sel(ISEL), .in(1'b1), .out_1(C_SEL), .out_2(C_VAL), .out_3(JS));  // open: out_0
  Demultiplexer #(.Selector_Bits(3)) demultiplexer_2 (
    .sel(DOUT), .in(1'b1), .out_1(demultiplexer_2_out_1), .out_2(demultiplexer_2_out_2),
    .out_3(demultiplexer_2_out_3), .out_4(demultiplexer_2_out_4));  // open: out_0, out_5, out_6, out_7
  LED ST1_JP1 (.in(IWORD[12]));
  LED ST0_JP0 (.in(IWORD[11]));
  and and_1 (and_1_out, ~JMP_C, CARRY);  // And
  and and_2 (and_2_out, ~JMP_Z, ZERO);  // And
  not not_1 (not_1_out, JS);
  not not_2 (nA_DOUT, demultiplexer_2_out_1);
  not not_3 (nMEM_DOUT, demultiplexer_2_out_2);
  not not_4 (nSUM_DOUT, demultiplexer_2_out_3);
  not not_5 (nROM_DOUT, demultiplexer_2_out_4);
  LED DT2 (.in(DOUT[2]));
  LED DT1 (.in(DOUT[1]));
  ROM #(.AddrBits(8), .Bits(16)) rom_1 (.A(PC_out), .sel(1'b1), .D(rom_1_d));
  or or_1 (nPC_ST, not_1_out, JMP_EN);
  LED DT0 (.in(DOUT[0]));
  LED D7 (.in(IWORD[7]));
  LED D6 (.in(IWORD[6]));
  DipSwitch dipswitch_1 (.out(dipswitch_8_out[7]));
  DipSwitch dipswitch_2 (.out(dipswitch_8_out[6]));
  D_FF #(.Bits(16)) CTRL (.D(rom_1_d), .C(CLK1), .Q({ISEL, IWORD[13:11], DOUT, IWORD[7:0]}));  // open: nQ
  or or_2 (or_2_out, and_1_out, and_2_out);
  LED D5 (.in(IWORD[5]));
  LED D4 (.in(IWORD[4]));
  DipSwitch dipswitch_3 (.out(dipswitch_8_out[5]));
  DipSwitch dipswitch_4 (.out(dipswitch_8_out[4]));
  not not_6 (not_6_out, or_2_out);
  Demultiplexer #(.Selector_Bits(2)) demultiplexer_3 (
    .sel(JMP_SEL), .in(1'b1), .out_1(demultiplexer_3_out_1), .out_2(demultiplexer_3_out_2),
    .out_3(demultiplexer_3_out_3));  // open: out_0
  not not_7 (JMP_C, demultiplexer_3_out_1);
  not not_8 (not_8_out, demultiplexer_3_out_2);
  not not_9 (not_9_out, demultiplexer_3_out_3);
  Demultiplexer #(.Selector_Bits(3)) demultiplexer_4 (
    .sel(ST), .in(1'b1), .out_1(demultiplexer_4_out_1), .out_2(demultiplexer_4_out_2),
    .out_3(demultiplexer_4_out_3), .out_4(demultiplexer_4_out_4), .out_7(demultiplexer_4_out_7));  // open: out_0, out_5, out_6
  not not_10 (nA_ST, demultiplexer_4_out_1);
  not not_11 (nMEM_ST, demultiplexer_4_out_2);
  not not_12 (nSUM_ST, demultiplexer_4_out_3);
  not not_13 (nMAR_ST, demultiplexer_4_out_4);
  not not_14 (nDISP_ST, demultiplexer_4_out_7);
  LED D3 (.in(IWORD[3]));
  LED D2 (.in(IWORD[2]));
  DipSwitch dipswitch_5 (.out(dipswitch_8_out[3]));
  DipSwitch dipswitch_6 (.out(dipswitch_8_out[2]));
  Demultiplexer #(.Bits(3)) demultiplexer_5 (
    .sel(JS), .in(IWORD[13:11]), .out_0(ST), .out_1({demultiplexer_5_out_1[2], JMP_SEL}));
  Multiplexer multiplexer_1 (.sel(not_15_out), .in_0(or_2_out), .in_1(not_6_out), .out(JMP_EN));
  LED D1 (.in(IWORD[1]));
  LED D0 (.in(IWORD[0]));
  DipSwitch dipswitch_7 (.out(dipswitch_8_out[1]));
  DipSwitch dipswitch_8 (.out(dipswitch_8_out[0]));
  assign DATA = ~nROM_DOUT ? IWORD[7:0] : 8'bz;  // DriverInvSel driverinvsel_1
  not not_15 (not_15_out, JMP_POS);
  and and_3 (JMP_POS, not_8_out, JMP_C);
  assign DATA = ~1'b1 ? dipswitch_8_out : 8'bz;  // DriverInvSel driverinvsel_2
  and and_4 (JMP_Z, not_9_out, not_8_out);
  not not_16 (not_16_out, Clock);
  PullDown pulldown_1 (.out(Clock));
  T_FF #(.withEnable("false")) t_ff_1 (.C(not_16_out), .Q(t_ff_1_q), .nQ(t_ff_1_nq));
  and and_5 (CLK1, Clock, t_ff_1_q);
  and and_6 (CLK2, t_ff_1_nq, Clock);
  Seven_Seg seven_seg_1 (
    .a(H_d[0]), .b(H_d[1]), .c(H_d[2]), .d(H_d[3]), .e(H_d_2[0]), .f(H_d_2[1]), .g(H_d_2[2]), .dp(H_d_2[3]));
  Seven_Seg seven_seg_2 (
    .a(T_d[0]), .b(T_d[1]), .c(T_d[2]), .d(T_d[3]), .e(T_d_2[0]), .f(T_d_2[1]), .g(T_d_2[2]), .dp(T_d_2[3]));
  PullDown #(.Bits(8)) pulldown_2 (.out(DATA));
  Register #(.Bits(8)) A (.D(DATA), .C(CLK2), .en(~nA_ST), .Q(A_q));
  Multiplexer multiplexer_2 (.sel(C_SEL), .in_0(C_VAL), .in_1(CARRY), .out(multiplexer_2_out));
  BitExtender #(.inputBits(1), .outputBits(8)) bitextender_1 (.in(C_VAL), .out(bitextender_1_out));
  Register #(.Bits(8)) MAR (.D(DATA), .C(CLK2), .en(~nMAR_ST), .Q(MAR_q));
  and and_7 (and_7_out, nMEM_DOUT, nMEM_ST);
  Seven_Seg seven_seg_3 (
    .a(O_d[0]), .b(O_d[1]), .c(O_d[2]), .d(O_d[3]), .e(O_d_2[4]), .f(O_d_2[5]), .g(O_d_2[6]), .dp(O_d_2[7]));
  assign xor_1_out = DATA ^ bitextender_1_out;  // XOr xor_1, 8 bits wide
  nand nand_1 (nand_1_out, MAR_q[6], and_7_out);
  Register #(.Bits(8)) DISP (.D(DATA), .C(CLK2), .en(~nDISP_ST), .Q(DISP_q));
  assign DATA = ~nA_DOUT ? A_q : 8'bz;  // DriverInvSel driverinvsel_3
  Add #(.Bits(8)) add_1 (.a(A_q), .b(xor_1_out), .c_i(multiplexer_2_out), .s(add_1_s), .c_o(and_8_out[0]));
  or or_3 (or_3_out, 1'b0, MAR_q[6]);
  ROM #(.AddrBits(8), .Bits(8)) H (.A(DISP_q), .sel(1'b1), .D({H_d_2, H_d}));
  ROM #(.AddrBits(8), .Bits(8)) T (.A(DISP_q), .sel(1'b1), .D({T_d_2, T_d}));
  ROM #(.AddrBits(8), .Bits(8)) O (.A(DISP_q), .sel(1'b1), .D({O_d_2, O_d}));
  Demultiplexer #(.Selector_Bits(3)) demultiplexer_6 (
    .sel(MAR_q[2:0]), .in(nand_1_out));  // open: out_0, out_1, out_2, out_3, out_4, out_5, out_6, out_7
  assign nor_1_out = ~(add_1_s[7:6] | add_1_s[5:4]);  // NOr nor_1, 2 bits wide
  assign nor_2_out = ~(add_1_s[3:2] | add_1_s[1:0]);  // NOr nor_2, 2 bits wide
  RAMSinglePortSel #(.AddrBits(6), .Bits(8)) MEM__64x8 (
    .A(MAR_q[5:0]), .CS(~or_3_out), .WE(~nMEM_ST), .OE(~nMEM_DOUT), .D(MEM__64x8_d));
  PullDown #(.Bits(8)) pulldown_3 (.out(MEM__64x8_d));
  BusSplitter #(.Bits(8)) bussplitter_1 (
    .D(MEM__64x8_d), .OE(not_17_out), .D0(bussplitter_1_d0), .D1(bussplitter_1_d1), .D2(bussplitter_1_d2),
    .D3(bussplitter_1_d3), .D4(bussplitter_1_d4), .D5(bussplitter_1_d5), .D6(bussplitter_1_d6),
    .D7(bussplitter_1_d7));
  not not_17 (not_17_out, nMEM_DOUT);
  PullDown pulldown_4 (.out(bussplitter_1_d0));
  PullDown pulldown_5 (.out(bussplitter_1_d1));
  PullDown pulldown_6 (.out(bussplitter_1_d2));
  PullDown pulldown_7 (.out(bussplitter_1_d3));
  and and_8 (and_8_out[1], nor_1_out[0], nor_1_out[1], nor_2_out[0], nor_2_out[1]);
  not not_18 (not_18_out, nMEM_DOUT);
  PullDown pulldown_8 (.out(bussplitter_1_d4));
  PullDown pulldown_9 (.out(bussplitter_1_d5));
  PullDown pulldown_10 (.out(bussplitter_1_d6));
  PullDown pulldown_11 (.out(bussplitter_1_d7));
  // _74245 _74245_1: pin names not known; wires that end beside it: not_18_out, 1'b1, 1'b0, bussplitter_1_d0, bussplitter_1_d1, bussplitter_1_d2, bussplitter_1_d3, bussplitter_1_d4, bussplitter_1_d5, bussplitter_1_d6, bussplitter_1_d7, 1'b0, _74245_1_p13, _74245_1_p14, _74245_1_p15, _74245_1_p16, _74245_1_p17, _74245_1_p18, _74245_1_p19, _74245_1_p20
  Register #(.Bits(2)) CZ (.D(and_8_out), .C(CLK2), .en(~nSUM_ST), .Q({ZERO, CARRY}));
  Register #(.Bits(8)) SUM (.D(add_1_s), .C(CLK2), .en(~nSUM_ST), .Q(SUM_q));
  PullDown pulldown_12 (.out(_74245_1_p20));
  PullDown pulldown_13 (.out(_74245_1_p19));
  PullDown pulldown_14 (.out(_74245_1_p18));
  PullDown pulldown_15 (.out(_74245_1_p17));
  PullDown pulldown_16 (.out(_74245_1_p16));
  assign DATA = ~nSUM_DOUT ? SUM_q : 8'bz;  // DriverInvSel driverinvsel_4
  BusSplitter #(.Bits(8)) bussplitter_2 (
    .D(DATA), .OE(nMEM_DOUT), .D0(_74245_1_p13), .D1(_74245_1_p14), .D2(_74245_1_p15), .D3(_74245_1_p16),
    .D4(_74245_1_p17), .D5(_74245_1_p18), .D6(_74245_1_p19), .D7(_74245_1_p20));
  PullDown pulldown_17 (.out(_74245_1_p15));
  PullDown pulldown_18 (.out(_74245_1_p14));
  PullDown pulldown_19 (.out(_74245_1_p13));

  // Other names for the same wires on the sheet: CLK_1 = CLK1; CLK_2 = CLK2; IWORD (some bits) = {ISEL, DOUT}

  // Notes on the sheet:
  //   Clock: Hz: 10
  //   PANEL0
  //   ATLAS PDC-8
  //   CTRL0
  //   CTRL1
  //   contents of rom_1 (hex, n*v repeats v):
  //   1800,2400,c01,1401,cc00,3900,1a00,1300,cc00,3a00,1a00,b00,c404
  //   PANEL1
  //   ALU
  //   MEM
  //   contents of H (hex, n*v repeats v):
  //   100*0,100*6,56*5b
  //   contents of T (hex, n*v repeats v):
  //   10*0,10*6,10*5b,10*4f,10*66,10*6d,10*7d,10*7,10*7f,10*6f,10*3f
  //   ,10*6,10*5b,10*4f,10*66,10*6d,10*7d,10*7,10*7f,10*6f,10*3f,10*6
  //   ,10*5b,10*4f,10*66,6*6d
  //   contents of O (hex, n*v repeats v):
  //   3f,6,5b,4f,66,6d,7d,7,7f,6f,3f,6,5b,4f,66,6d,7d,7,7f,6f,3f,6,5b
  //   ,4f,66,6d,7d,7,7f,6f,3f,6,5b,4f,66,6d,7d,7,7f,6f,3f,6,5b,4f,66
  //   ,6d,7d,7,7f,6f,3f,6,5b,4f,66,6d,7d,7,7f,6f,3f,6,5b,4f,66,6d,7d
  //   ,7,7f,6f,3f,6,5b,4f,66,6d,7d,7,7f,6f,3f,6,5b,4f,66,6d,7d,7,7f
  //   ,6f,3f,6,5b,4f,66,6d,7d,7,7f,6f,3f,6,5b,4f,66,6d,7d,7,7f,6f,3f
  //   ,6,5b,4f,66,6d,7d,7,7f,6f,3f,6,5b,4f,66,6d,7d,7,7f,6f,3f,6,5b
  //   ,4f,66,6d,7d,7,7f,6f,3f,6,5b,4f,66,6d,7d,7,7f,6f,3f,6,5b,4f,66
  //   ,6d,7d,7,7f,6f,3f,6,5b,4f,66,6d,7d,7,7f,6f,3f,6,5b,4f,66,6d,7d
  //   ,7,7f,6f,3f,6,5b,4f,66,6d,7d,7,7f,6f,3f,6,5b,4f,66,6d,7d,7,7f
  //   ,6f,3f,6,5b,4f,66,6d,7d,7,7f,6f,3f,6,5b,4f,66,6d,7d,7,7f,6f,3f
  //   ,6,5b,4f,66,6d,7d,7,7f,6f,3f,6,5b,4f,66,6d,7d,7,7f,6f,3f,6,5b
  //   ,4f,66,6d,7d,7,7f,6f,3f,6,5b,4f,66,6d
endmodule
