// Digital circuit CPU 8.dig as structural Verilog
module CPU_8 (
  input  Clock,
  input  RST,
  input  DMA,
  input  nWAIT,
  input  in_7,
  input  in_8,
  input  in_9,
  input  in_10,
  output CLK1,
  output CLK2
);

  wire and_1_out, and_2_out, and_8_out, and_9_out, and_10_out, and_14_out, and_15_out, and_16_out,
       and_17_out, and_20_out, COND_C, COND_N, COND_NEG, COND_POS, COND_RES, COND_Z, CONV_V,
       demultiplexer_1_out_0, demultiplexer_1_out_1, demultiplexer_2_out_1, demultiplexer_2_out_2,
       demultiplexer_2_out_3, demultiplexer_2_out_4, demultiplexer_2_out_5, demultiplexer_4_out_0,
       demultiplexer_4_out_1, demultiplexer_4_out_2, demultiplexer_5_out_1, demultiplexer_5_out_2,
       demultiplexer_5_out_3, demultiplexer_5_out_4, demultiplexer_5_out_5, demultiplexer_5_out_6,
       demultiplexer_5_out_7, demultiplexer_6_out_0, demultiplexer_6_out_1, demultiplexer_6_out_2,
       demultiplexer_6_out_3, demultiplexer_6_out_4, demultiplexer_6_out_5, demultiplexer_6_out_6,
       demultiplexer_6_out_7, demultiplexer_7_out_0, demultiplexer_7_out_1, demultiplexer_8_out_1,
       demultiplexer_8_out_2, demultiplexer_8_out_3, demultiplexer_8_out_4, demultiplexer_8_out_5,
       demultiplexer_9_out_0, demultiplexer_9_out_1, demultiplexer_9_out_2, demultiplexer_9_out_3,
       demultiplexer_9_out_4, demultiplexer_9_out_5, demultiplexer_9_out_6, demultiplexer_9_out_7,
       demultiplexer_10_out_0, demultiplexer_10_out_1, demultiplexer_10_out_2, demultiplexer_10_out_3,
       demultiplexer_10_out_4, demultiplexer_10_out_5, demultiplexer_10_out_6, demultiplexer_10_out_7,
       demultiplexer_11_out_0, demultiplexer_11_out_1, demultiplexer_11_out_2, demultiplexer_12_out_1,
       demultiplexer_12_out_2, demultiplexer_12_out_3, demultiplexer_12_out_4, demultiplexer_12_out_5,
       demultiplexer_12_out_6, demultiplexer_12_out_7, demultiplexer_13_out_0, demultiplexer_13_out_1,
       demultiplexer_13_out_2, demultiplexer_13_out_3, demultiplexer_13_out_4, demultiplexer_13_out_5,
       demultiplexer_13_out_6, demultiplexer_13_out_7, demultiplexer_14_out_0, demultiplexer_14_out_1,
       demultiplexer_15_out_1, demultiplexer_15_out_2, demultiplexer_15_out_3, demultiplexer_15_out_4,
       DMA_ack, FLAG_C, FLAG_V, IRQ_ack, IRQ_en, IRQ_FTdat, IRQ_REQ, nA_ALUin, nA_DATout, nA_st, nB_DATout,
       nB_st, nBASE_st, nBIT_DATout, nC_DATout, nC_Fst, nC_st, nD_DATout, nD_st, nF_ALUin, nF_DATin,
       nF_DATout, nIR_st, nIRQ_Fst, nIX_DATout, nIX_en, nIX_st, nIY_DATout, nIY_en, nIY_st, nLSH_DATout,
       nMAR_ADSout, nMARH_st, nMARL_st, nMEM_DATout, nMEM_st, nMSK_st, nNZ_Fst, nOFF_ADSout, nOFF_DATout,
       nor_1_out, nor_2_out, nor_3_out, nor_4_out, nor_5_out, nor_6_out, nor_7_out, nor_8_out, not_1_out,
       not_2_out, not_3_out, not_4_out, not_5_out, not_12_out, not_19_out, not_20_out, not_21_out,
       not_22_out, not_23_out, not_38_out, not_39_out, not_40_out, not_41_out, not_42_out, not_43_out,
       not_44_out, not_45_out, not_46_out, not_47_out, not_48_out, not_49_out, not_50_out, not_58_out,
       not_59_out, not_70_out, not_81_out, not_82_out, not_83_out, nPC_ADSout, nPC_DATout, nPC_en, nPC_st,
       nREL_st, nRSH_DATout, nRST_ADSout, nSEQ_en, nSEQ_st, nSP_ADSout, nSP_DATout, nSP_en, nSP_st,
       nSUM_DATout, nSUM_st, nTMEM_DATout, nTMEM_st, nV_Fst, nWORD_DATout, or_1_out, or_3_out, or_4_out,
       or_5_out, or_6_out, or_7_out, or_8_out, or_9_out, or_10_out, SEQ_val, SP_dir, t_ff_1_nq, t_ff_1_q,
       TEMP_clr, \Σ_Csel , \Σ_Cval , \Σ_M ;
  wire [1:0] FLAG_NZ;
  wire [2:0] AOUT_sel, COND_sel;
  wire [3:0] alu_1_c_f, driverinvsel_15_out, FST_sel, \µSEQ_out , \Σ_sel ;
  wire [4:0] DOUT_sel, ST_sel;
  wire [6:4] DMA_q;
  wire [7:0] MARH_out, MARL_out, MSK_q;
  wire [10:0] IR_q;
  wire [15:0] A_q, ADDRESS_in, ADDRESS_out, alu_1_sum, B_q, barrelshifter_1_out, barrelshifter_2_out,
       BASE_out, C_q, D_q, DATA_in, DATA_out, driverinvsel_8_out, IX_out, IY_out, MEMDATA_in, OFFSET_s,
       PC_out, REL_out, SP_out, SUM_out, TMEM_out;
  wire [47:0] \µCODE_d ;
  wire [47:29] CTRL_q;

  Demultiplexer demultiplexer_1 (
    .sel(FST_sel[3]), .in(1'b1), .out_0(demultiplexer_1_out_0), .out_1(demultiplexer_1_out_1));
  assign ADDRESS_out = ~nRST_ADSout ? {16{1'b1}} : 16'bz;  // DriverInvSel driverinvsel_1
  assign DATA_out = ~nWORD_DATout ? {16{1'b1}} : 16'bz;  // DriverInvSel driverinvsel_2
  assign DATA_out = ~nBIT_DATout ? 16'h1 : 16'bz;  // DriverInvSel driverinvsel_3
  Register #(.Bits(8)) MSK (.D(MEMDATA_in[7:0]), .C(CLK2), .en(~nMSK_st), .Q(MSK_q));
  not not_1 (not_1_out, COND_RES);
  Register IRQ (.D(DATA_in[4]), .C(CLK2), .en(~nIRQ_Fst), .Q(IRQ_FTdat));
  Demultiplexer #(.Selector_Bits(3)) demultiplexer_2 (
    .sel(FST_sel[2:0]), .in(demultiplexer_1_out_0), .out_1(demultiplexer_2_out_1),
    .out_2(demultiplexer_2_out_2), .out_3(demultiplexer_2_out_3), .out_4(demultiplexer_2_out_4),
    .out_5(demultiplexer_2_out_5));  // open: out_0, out_6, out_7
  Demultiplexer #(.Selector_Bits(3)) demultiplexer_3 (
    .sel(FST_sel[2:0]), .in(demultiplexer_1_out_1));  // open: out_0, out_1, out_2, out_3, out_4, out_5, out_6, out_7
  and and_1 (and_1_out, nSEQ_st, not_1_out);
  not not_2 (not_2_out, demultiplexer_2_out_1);
  not not_3 (not_3_out, demultiplexer_2_out_2);
  not not_4 (not_4_out, demultiplexer_2_out_3);
  not not_5 (not_5_out, demultiplexer_2_out_4);
  not not_6 (nIRQ_Fst, demultiplexer_2_out_5);
  and and_2 (and_2_out, IRQ_REQ, IRQ_FTdat);
  PullDown #(.Bits(16)) pulldown_1 (.out(ADDRESS_out));
  PullDown #(.Bits(16)) pulldown_2 (.out(DATA_out));
  PullDown #(.Bits(16)) pulldown_3 (.out(DATA_out));
  nor nor_1 (nor_1_out, MSK_q[0], 1'b0);
  nor nor_2 (nor_2_out, MSK_q[1], 1'b0);
  nor nor_3 (nor_3_out, MSK_q[2], 1'b0);
  nor nor_4 (nor_4_out, MSK_q[3], 1'b0);
  nor nor_5 (nor_5_out, MSK_q[4], 1'b0);
  nor nor_6 (nor_6_out, MSK_q[5], 1'b0);
  nor nor_7 (nor_7_out, MSK_q[6], 1'b0);
  nor nor_8 (nor_8_out, MSK_q[7], 1'b0);
  and and_3 (nNZ_Fst, not_2_out, not_5_out);
  and and_4 (nV_Fst, not_3_out, not_5_out);
  and and_5 (nC_Fst, not_4_out, not_5_out);
  CounterPreset #(.Bits(4)) \u_µSEQ  (
    .en(~nSEQ_en), .C(CLK2), .dir(1'b0), .in({3'b000, SEQ_val}), .ld(~and_1_out), .clr(1'b0), .out(\µSEQ_out ));  // open: ovf
  Register u_DMA (.D(DMA), .C(CLK2), .en(~IRQ_en), .Q(DMA_q[4]));
  Register RESET (.D(RST), .C(CLK2), .en(~IRQ_en), .Q(DMA_q[5]));
  Register IRQ_2 (.D(and_2_out), .C(CLK2), .en(~IRQ_en), .Q(DMA_q[6]));
  Register #(.Bits(11)) IR (.D(DATA_in[10:0]), .C(CLK2), .en(~nIR_st), .Q(IR_q));
  PriorityEncoder #(.Selector_Bits(3)) FAULT (
    .in0(1'b0), .in1(1'b0), .in2(1'b0), .in3(1'b0), .in4(1'b0), .in5(1'b0), .in6(1'b0), .in7(1'b0));  // open: num, any
  PriorityEncoder #(.Selector_Bits(3)) IRQ0 (
    .in0(nor_1_out), .in1(nor_2_out), .in2(nor_3_out), .in3(nor_4_out), .in4(nor_5_out), .in5(nor_6_out),
    .in6(nor_7_out), .in7(nor_8_out), .any(IRQ_REQ));  // open: num
  ROM #(.AddrBits(18), .Bits(48)) \u_µCODE  (.A({IR_q, DMA_q, \µSEQ_out }), .sel(1'b1), .D(\µCODE_d ));
  Demultiplexer #(.Selector_Bits(2)) demultiplexer_4 (
    .sel(ST_sel[4:3]), .in(1'b1), .out_0(demultiplexer_4_out_0), .out_1(demultiplexer_4_out_1),
    .out_2(demultiplexer_4_out_2));  // open: out_3
  D_FF #(.Bits(48)) CTRL (
    .D(\µCODE_d ), .C(CLK1),
    .Q({CTRL_q[47:40], nA_ALUin, IRQ_ack, DMA_ack, CTRL_q[36], TEMP_clr, SEQ_val, CTRL_q[33:32], nF_ALUin, CTRL_q[30:29], SP_dir, COND_POS, \Σ_Cval , \Σ_Csel , \Σ_M , \Σ_sel , COND_sel, FST_sel, AOUT_sel, DOUT_sel, ST_sel}));  // open: nQ
  Demultiplexer #(.Selector_Bits(3)) demultiplexer_5 (
    .sel(ST_sel[2:0]), .in(demultiplexer_4_out_0), .out_1(demultiplexer_5_out_1),
    .out_2(demultiplexer_5_out_2), .out_3(demultiplexer_5_out_3), .out_4(demultiplexer_5_out_4),
    .out_5(demultiplexer_5_out_5), .out_6(demultiplexer_5_out_6), .out_7(demultiplexer_5_out_7));  // open: out_0
  Demultiplexer #(.Selector_Bits(3)) demultiplexer_6 (
    .sel(ST_sel[2:0]), .in(demultiplexer_4_out_1), .out_0(demultiplexer_6_out_0),
    .out_1(demultiplexer_6_out_1), .out_2(demultiplexer_6_out_2), .out_3(demultiplexer_6_out_3),
    .out_4(demultiplexer_6_out_4), .out_5(demultiplexer_6_out_5), .out_6(demultiplexer_6_out_6),
    .out_7(demultiplexer_6_out_7));
  Demultiplexer #(.Selector_Bits(3)) demultiplexer_7 (
    .sel(ST_sel[2:0]), .in(demultiplexer_4_out_2), .out_0(demultiplexer_7_out_0),
    .out_1(demultiplexer_7_out_1));  // open: out_2, out_3, out_4, out_5, out_6, out_7
  Demultiplexer #(.Selector_Bits(3)) demultiplexer_8 (
    .sel(AOUT_sel), .in(1'b1), .out_1(demultiplexer_8_out_1), .out_2(demultiplexer_8_out_2),
    .out_3(demultiplexer_8_out_3), .out_4(demultiplexer_8_out_4), .out_5(demultiplexer_8_out_5));  // open: out_0, out_6, out_7
  not not_7 (nA_st, demultiplexer_5_out_1);
  not not_8 (nB_st, demultiplexer_5_out_2);
  not not_9 (nC_st, demultiplexer_5_out_3);
  not not_10 (nD_st, demultiplexer_5_out_4);
  not not_11 (nSP_st, demultiplexer_5_out_5);
  not not_12 (not_12_out, demultiplexer_5_out_6);
  not not_13 (nIX_st, demultiplexer_5_out_7);
  not not_14 (nIY_st, demultiplexer_6_out_0);
  not not_15 (nIR_st, demultiplexer_6_out_1);
  not not_16 (nREL_st, demultiplexer_6_out_2);
  not not_17 (nBASE_st, demultiplexer_6_out_3);
  not not_18 (nSUM_st, demultiplexer_6_out_4);
  not not_19 (not_19_out, demultiplexer_6_out_5);
  not not_20 (not_20_out, demultiplexer_6_out_6);
  not not_21 (not_21_out, demultiplexer_6_out_7);
  not not_22 (not_22_out, demultiplexer_7_out_0);
  not not_23 (not_23_out, demultiplexer_7_out_1);
  not not_24 (nSP_ADSout, demultiplexer_8_out_1);
  not not_25 (nPC_ADSout, demultiplexer_8_out_2);
  not not_26 (nOFF_ADSout, demultiplexer_8_out_3);
  not not_27 (nMAR_ADSout, demultiplexer_8_out_4);
  not not_28 (nRST_ADSout, demultiplexer_8_out_5);
  not not_29 (nSP_en, CTRL_q[29]);
  not not_30 (nPC_en, CTRL_q[30]);
  not not_31 (nSEQ_en, CTRL_q[32]);
  not not_32 (nSEQ_st, CTRL_q[33]);
  not not_33 (IRQ_en, CTRL_q[36]);
  not not_34 (nIX_en, CTRL_q[40]);
  not not_35 (nIY_en, CTRL_q[41]);
  and and_6 (nMARH_st, not_19_out, not_22_out);
  and and_7 (nMARL_st, not_23_out, not_19_out);
  not not_36 (COND_NEG, COND_POS);
  not not_37 (nF_DATin, nF_ALUin);
  and and_8 (and_8_out, DMA_ack, in_10);
  and and_9 (and_9_out, DMA_ack, in_8);
  and and_10 (and_10_out, in_7, DMA_ack);
  not not_38 (not_38_out, not_48_out);
  and and_11 (nPC_st, not_39_out, not_12_out);
  not not_39 (not_39_out, and_8_out);
  and and_12 (nMEM_st, not_40_out, not_20_out);
  not not_40 (not_40_out, and_9_out);
  and and_13 (nTMEM_st, not_21_out, not_41_out);
  not not_41 (not_41_out, and_10_out);
  Demultiplexer #(.Selector_Bits(3)) demultiplexer_9 (
    .sel(ADDRESS_in[15:13]), .in(1'b1), .out_0(demultiplexer_9_out_0), .out_1(demultiplexer_9_out_1),
    .out_2(demultiplexer_9_out_2), .out_3(demultiplexer_9_out_3), .out_4(demultiplexer_9_out_4),
    .out_5(demultiplexer_9_out_5), .out_6(demultiplexer_9_out_6), .out_7(demultiplexer_9_out_7));
  not not_42 (not_42_out, demultiplexer_9_out_0);
  not not_43 (not_43_out, demultiplexer_9_out_1);
  not not_44 (not_44_out, demultiplexer_9_out_2);
  not not_45 (not_45_out, demultiplexer_9_out_3);
  not not_46 (not_46_out, demultiplexer_9_out_4);
  not not_47 (not_47_out, demultiplexer_9_out_5);
  not not_48 (not_48_out, demultiplexer_9_out_6);
  not not_49 (not_49_out, demultiplexer_9_out_7);
  Demultiplexer #(.Selector_Bits(3)) demultiplexer_10 (
    .sel(ADDRESS_in[6:4]), .in(not_38_out), .out_0(demultiplexer_10_out_0), .out_1(demultiplexer_10_out_1),
    .out_2(demultiplexer_10_out_2), .out_3(demultiplexer_10_out_3), .out_4(demultiplexer_10_out_4),
    .out_5(demultiplexer_10_out_5), .out_6(demultiplexer_10_out_6), .out_7(demultiplexer_10_out_7));
  not not_50 (not_50_out, demultiplexer_10_out_0);
  // Not not_51 has open pins: in=demultiplexer_10_out_1, out=open
  // Not not_52 has open pins: in=demultiplexer_10_out_2, out=open
  // Not not_53 has open pins: in=demultiplexer_10_out_3, out=open
  // Not not_54 has open pins: in=demultiplexer_10_out_4, out=open
  // Not not_55 has open pins: in=demultiplexer_10_out_5, out=open
  // Not not_56 has open pins: in=demultiplexer_10_out_6, out=open
  // Not not_57 has open pins: in=demultiplexer_10_out_7, out=open
  and and_14 (and_14_out, ~COND_N, FLAG_NZ[0]);  // And
  and and_15 (and_15_out, ~COND_Z, FLAG_NZ[1]);  // And
  or or_1 (or_1_out, not_42_out, not_43_out, not_44_out, not_45_out, not_46_out, not_47_out);
  or or_2 (nMSK_st, nMEM_st, not_50_out);
  and and_16 (and_16_out, ~CONV_V, FLAG_V);  // And
  not not_58 (not_58_out, Clock);
  PullDown pulldown_4 (.out(Clock));
  Demultiplexer #(.Selector_Bits(2)) demultiplexer_11 (
    .sel(DOUT_sel[4:3]), .in(1'b1), .out_0(demultiplexer_11_out_0), .out_1(demultiplexer_11_out_1),
    .out_2(demultiplexer_11_out_2));  // open: out_3
  or or_3 (or_3_out, and_14_out, and_15_out);
  and and_17 (and_17_out, ~COND_C, ~FLAG_C);  // And
  T_FF #(.withEnable("false")) t_ff_1 (.C(not_58_out), .Q(t_ff_1_q), .nQ(t_ff_1_nq));
  or or_4 (or_4_out, and_16_out, and_17_out);
  and and_18 (CLK1, Clock, t_ff_1_q);
  and and_19 (CLK2, t_ff_1_nq, ~nWAIT, Clock);  // And
  Demultiplexer #(.Selector_Bits(3)) demultiplexer_12 (
    .sel(DOUT_sel[2:0]), .in(demultiplexer_11_out_0), .out_1(demultiplexer_12_out_1),
    .out_2(demultiplexer_12_out_2), .out_3(demultiplexer_12_out_3), .out_4(demultiplexer_12_out_4),
    .out_5(demultiplexer_12_out_5), .out_6(demultiplexer_12_out_6), .out_7(demultiplexer_12_out_7));  // open: out_0
  Demultiplexer #(.Selector_Bits(3)) demultiplexer_13 (
    .sel(DOUT_sel[2:0]), .in(demultiplexer_11_out_1), .out_0(demultiplexer_13_out_0),
    .out_1(demultiplexer_13_out_1), .out_2(demultiplexer_13_out_2), .out_3(demultiplexer_13_out_3),
    .out_4(demultiplexer_13_out_4), .out_5(demultiplexer_13_out_5), .out_6(demultiplexer_13_out_6),
    .out_7(demultiplexer_13_out_7));
  Demultiplexer #(.Selector_Bits(3)) demultiplexer_14 (
    .sel(DOUT_sel[2:0]), .in(demultiplexer_11_out_2), .out_0(demultiplexer_14_out_0),
    .out_1(demultiplexer_14_out_1));  // open: out_2, out_3, out_4, out_5, out_6, out_7
  Demultiplexer #(.Selector_Bits(3)) demultiplexer_15 (
    .sel(COND_sel), .in(1'b1), .out_1(demultiplexer_15_out_1), .out_2(demultiplexer_15_out_2),
    .out_3(demultiplexer_15_out_3), .out_4(demultiplexer_15_out_4));  // open: out_0, out_5, out_6, out_7
  ROM #(.AddrBits(16), .Bits(16)) ROM_16x64k (.A(ADDRESS_in), .sel(not_59_out), .D(MEMDATA_in));
  not not_59 (not_59_out, not_49_out);
  RAMSinglePortSel #(.AddrBits(16), .Bits(16)) RAM0_16x64k (
    .A(ADDRESS_in), .CS(~or_1_out), .WE(~nMEM_st), .OE(~nMEM_DATout), .D(MEMDATA_in));
  not not_60 (nA_DATout, demultiplexer_12_out_1);
  not not_61 (nB_DATout, demultiplexer_12_out_2);
  not not_62 (nC_DATout, demultiplexer_12_out_3);
  not not_63 (nD_DATout, demultiplexer_12_out_4);
  not not_64 (nSP_DATout, demultiplexer_12_out_5);
  not not_65 (nPC_DATout, demultiplexer_12_out_6);
  not not_66 (nIX_DATout, demultiplexer_12_out_7);
  not not_67 (nIY_DATout, demultiplexer_13_out_0);
  not not_68 (nF_DATout, demultiplexer_13_out_1);
  not not_69 (nSUM_DATout, demultiplexer_13_out_2);
  not not_70 (not_70_out, demultiplexer_13_out_3);
  not not_71 (nLSH_DATout, demultiplexer_13_out_4);
  not not_72 (nRSH_DATout, demultiplexer_13_out_5);
  not not_73 (nWORD_DATout, demultiplexer_13_out_6);
  not not_74 (nBIT_DATout, demultiplexer_13_out_7);
  not not_75 (nTMEM_DATout, demultiplexer_14_out_0);
  not not_76 (nOFF_DATout, demultiplexer_14_out_1);
  not not_77 (COND_N, demultiplexer_15_out_1);
  not not_78 (COND_Z, demultiplexer_15_out_2);
  not not_79 (CONV_V, demultiplexer_15_out_3);
  not not_80 (COND_C, demultiplexer_15_out_4);
  or or_5 (or_5_out, or_3_out, or_4_out);
  PullDown #(.Bits(16)) pulldown_5 (.out(MEMDATA_in));
  not not_81 (not_81_out, or_5_out);
  and and_20 (and_20_out, DMA_ack, in_9);
  assign MEMDATA_in = ~nTMEM_DATout ? TMEM_out : 16'bz;  // DriverInvSel driverinvsel_4
  assign COND_RES = ~COND_POS ? or_5_out : 1'bz;  // DriverInvSel driverinvsel_5
  assign COND_RES = ~COND_NEG ? not_81_out : 1'bz;  // DriverInvSel driverinvsel_6
  not not_82 (not_82_out, and_20_out);
  assign DATA_out = ~nMEM_DATout ? MEMDATA_in : 16'bz;  // DriverInvSel driverinvsel_7
  and and_21 (nMEM_DATout, not_82_out, not_70_out);
  CounterPreset #(.Bits(16)) TMEM (
    .en(~1'b1), .C(CLK2), .dir(1'b0), .in(DATA_in), .ld(~nTMEM_st), .clr(TEMP_clr), .out(TMEM_out));  // open: ovf
  LED D15 (.in(DATA_in[15]));
  LED A15 (.in(ADDRESS_in[15]));
  Register #(.Bits(16)) A (.D(DATA_in), .C(CLK2), .en(~nA_st), .Q(A_q));
  LED D13 (.in(DATA_in[13]));
  LED D14 (.in(DATA_in[14]));
  LED A13 (.in(ADDRESS_in[13]));
  LED A14 (.in(ADDRESS_in[14]));
  assign driverinvsel_8_out = ~nA_ALUin ? A_q : 16'bz;  // DriverInvSel driverinvsel_8
  Register #(.Bits(16)) B (.D(DATA_in), .C(CLK2), .en(~nB_st), .Q(B_q));
  Register #(.Bits(16)) C (.D(DATA_in), .C(CLK2), .en(~nC_st), .Q(C_q));
  Register #(.Bits(16)) D (.D(DATA_in), .C(CLK2), .en(~nD_st), .Q(D_q));
  CounterPreset #(.Bits(16)) IX (
    .en(~1'b1), .C(CLK2), .dir(1'b0), .in(DATA_in), .ld(~nB_st), .clr(1'b0), .out(IX_out));  // open: ovf
  CounterPreset #(.Bits(16)) IY (
    .en(~1'b1), .C(CLK2), .dir(1'b0), .in(DATA_in), .ld(~nB_st), .clr(1'b0), .out(IY_out));  // open: ovf
  LED D12 (.in(DATA_in[12]));
  LED A12 (.in(ADDRESS_in[12]));
  PullDown #(.Bits(16)) pulldown_6 (.out(driverinvsel_8_out));
  LED D11 (.in(DATA_in[11]));
  LED A11 (.in(ADDRESS_in[11]));
  assign DATA_out = ~nA_DATout ? driverinvsel_8_out : 16'bz;  // DriverInvSel driverinvsel_9
  assign DATA_out = ~nB_DATout ? B_q : 16'bz;  // DriverInvSel driverinvsel_10
  assign DATA_out = ~nC_DATout ? C_q : 16'bz;  // DriverInvSel driverinvsel_11
  assign DATA_out = ~nD_DATout ? D_q : 16'bz;  // DriverInvSel driverinvsel_12
  assign DATA_out = ~nIX_DATout ? IX_out : 16'bz;  // DriverInvSel driverinvsel_13
  assign DATA_out = ~nIY_DATout ? IY_out : 16'bz;  // DriverInvSel driverinvsel_14
  LED D9 (.in(DATA_in[9]));
  LED D10 (.in(DATA_in[10]));
  LED A9 (.in(ADDRESS_in[9]));
  LED A10 (.in(ADDRESS_in[10]));
  PullDown #(.Bits(16)) pulldown_7 (.out(DATA_out));
  LED D8 (.in(DATA_in[8]));
  LED A8 (.in(ADDRESS_in[8]));
  PullDown #(.Bits(16)) pulldown_8 (.out(DATA_out));
  PullDown #(.Bits(16)) pulldown_9 (.out(DATA_out));
  PullDown #(.Bits(16)) pulldown_10 (.out(DATA_out));
  PullDown #(.Bits(16)) pulldown_11 (.out(DATA_out));
  PullDown #(.Bits(16)) pulldown_12 (.out(DATA_out));
  LED D7 (.in(DATA_in[7]));
  LED A7 (.in(ADDRESS_in[7]));
  LED D5 (.in(DATA_in[5]));
  LED D6 (.in(DATA_in[6]));
  LED A5 (.in(ADDRESS_in[5]));
  LED A6 (.in(ADDRESS_in[6]));
  ALU alu_1 (
    .Sum(alu_1_sum), .C_sel(\Σ_Csel ), .C_val(\Σ_Cval ), .nCin(FLAG_C), .A(driverinvsel_8_out),
    .Sel(\Σ_sel ), .B(DATA_in), .M(\Σ_M ), .C_f(alu_1_c_f[3]), .N_f(alu_1_c_f[2]), .Z_f(alu_1_c_f[1]),
    .V_f(alu_1_c_f[0]));
  LED D4 (.in(DATA_in[4]));
  LED A4 (.in(ADDRESS_in[4]));
  or or_6 (or_6_out, CLK2, TEMP_clr);
  assign driverinvsel_15_out = ~nF_DATin ? DATA_in[3:0] : 4'bz;  // DriverInvSel driverinvsel_15
  or or_7 (or_7_out, CLK2, TEMP_clr);
  or or_8 (or_8_out, CLK2, TEMP_clr);
  LED D3 (.in(DATA_in[3]));
  LED A3 (.in(ADDRESS_in[3]));
  assign driverinvsel_15_out = ~nF_ALUin ? alu_1_c_f : 4'bz;  // DriverInvSel driverinvsel_16
  LED D1 (.in(DATA_in[1]));
  LED D2 (.in(DATA_in[2]));
  LED A1 (.in(ADDRESS_in[1]));
  LED A2 (.in(ADDRESS_in[2]));
  CounterPreset #(.Bits(16)) SUM (
    .en(~1'b1), .C(or_6_out), .dir(1'b0), .in(alu_1_sum), .ld(~nSUM_st), .clr(TEMP_clr), .out(SUM_out));  // open: ovf
  PullDown #(.Bits(4)) pulldown_13 (.out(driverinvsel_15_out));
  CounterPreset #(.Bits(16)) PC (
    .en(~nPC_en), .C(CLK2), .dir(1'b0), .in(DATA_in), .ld(~nPC_st), .clr(1'b0), .out(PC_out));  // open: ovf
  CounterPreset #(.Bits(16)) SP (
    .en(~nSP_en), .C(CLK2), .dir(SP_dir), .in(DATA_in), .ld(~nSP_st), .clr(1'b0), .out(SP_out));  // open: ovf
  CounterPreset #(.Bits(8)) MARH (
    .en(~1'b1), .C(or_7_out), .dir(1'b0), .in(DATA_in[15:8]), .ld(~nMARH_st), .clr(TEMP_clr), .out(MARH_out));  // open: ovf
  CounterPreset #(.Bits(8)) MARL (
    .en(~1'b1), .C(or_8_out), .dir(1'b0), .in(DATA_in[7:0]), .ld(~nMARL_st), .clr(TEMP_clr), .out(MARL_out));  // open: ovf
  LED D0 (.in(DATA_in[0]));
  LED A0 (.in(ADDRESS_in[0]));
  assign DATA_out = ~nSUM_DATout ? SUM_out : 16'bz;  // DriverInvSel driverinvsel_17
  Register #(.Bits(2)) NZ_F (.D(driverinvsel_15_out[1:0]), .C(CLK2), .en(~nNZ_Fst), .Q(FLAG_NZ));
  Register V_F (.D(driverinvsel_15_out[2]), .C(CLK2), .en(~nV_Fst), .Q(FLAG_V));
  Register nC_F (.D(driverinvsel_15_out[3]), .C(CLK2), .en(~nC_Fst), .Q(FLAG_C));
  assign ADDRESS_out = ~nPC_ADSout ? PC_out : 16'bz;  // DriverInvSel driverinvsel_18
  assign DATA_out = ~nPC_DATout ? PC_out : 16'bz;  // DriverInvSel driverinvsel_19
  assign ADDRESS_out = ~nSP_ADSout ? SP_out : 16'bz;  // DriverInvSel driverinvsel_20
  assign DATA_out = ~nSP_DATout ? SP_out : 16'bz;  // DriverInvSel driverinvsel_21
  LED V (.in(FLAG_V));
  LED C_2 (.in(not_83_out));
  not not_83 (not_83_out, FLAG_C);
  assign ADDRESS_out = ~nMAR_ADSout ? {MARH_out, MARL_out} : 16'bz;  // DriverInvSel driverinvsel_22
  LED Z (.in(FLAG_NZ[1]));
  PullDown #(.Bits(16)) pulldown_14 (.out(DATA_out));
  PullDown #(.Bits(16)) pulldown_15 (.out(DATA_out));
  PullDown #(.Bits(16)) pulldown_16 (.out(ADDRESS_out));
  LED N (.in(FLAG_NZ[0]));
  PullDown #(.Bits(16)) pulldown_17 (.out(ADDRESS_out));
  PullDown #(.Bits(16)) pulldown_18 (.out(ADDRESS_out));
  PullDown #(.Bits(16)) pulldown_19 (.out(DATA_out));
  assign DATA_out = ~nF_DATout ? {{11{1'b0}}, IRQ_FTdat, FLAG_C, FLAG_V, FLAG_NZ} : 16'bz;  // DriverInvSel driverinvsel_23
  PullDown #(.Bits(16)) pulldown_20 (.out(DATA_out));
  or or_9 (or_9_out, CLK2, TEMP_clr);
  or or_10 (or_10_out, CLK2, TEMP_clr);
  CounterPreset #(.Bits(16)) REL (
    .en(~1'b1), .C(or_9_out), .dir(1'b0), .in(DATA_in), .ld(~nREL_st), .clr(TEMP_clr), .out(REL_out));  // open: ovf
  CounterPreset #(.Bits(16)) BASE (
    .en(~1'b1), .C(or_10_out), .dir(1'b0), .in(DATA_in), .ld(~nBASE_st), .clr(TEMP_clr), .out(BASE_out));  // open: ovf
  DiodeForward diodeforward_1 (.in(ADDRESS_out[0]), .out(ADDRESS_in[0]));
  DiodeForward diodeforward_2 (.in(ADDRESS_out[1]), .out(ADDRESS_in[1]));
  DiodeForward diodeforward_3 (.in(ADDRESS_out[2]), .out(ADDRESS_in[2]));
  DiodeForward diodeforward_4 (.in(ADDRESS_out[3]), .out(ADDRESS_in[3]));
  DiodeForward diodeforward_5 (.in(ADDRESS_out[4]), .out(ADDRESS_in[4]));
  DiodeForward diodeforward_6 (.in(ADDRESS_out[5]), .out(ADDRESS_in[5]));
  DiodeForward diodeforward_7 (.in(ADDRESS_out[6]), .out(ADDRESS_in[6]));
  DiodeForward diodeforward_8 (.in(ADDRESS_out[7]), .out(ADDRESS_in[7]));
  DiodeForward diodeforward_9 (.in(ADDRESS_out[8]), .out(ADDRESS_in[8]));
  DiodeForward diodeforward_10 (.in(ADDRESS_out[9]), .out(ADDRESS_in[9]));
  DiodeForward diodeforward_11 (.in(ADDRESS_out[10]), .out(ADDRESS_in[10]));
  DiodeForward diodeforward_12 (.in(ADDRESS_out[11]), .out(ADDRESS_in[11]));
  DiodeForward diodeforward_13 (.in(ADDRESS_out[12]), .out(ADDRESS_in[12]));
  DiodeForward diodeforward_14 (.in(ADDRESS_out[13]), .out(ADDRESS_in[13]));
  DiodeForward diodeforward_15 (.in(ADDRESS_out[14]), .out(ADDRESS_in[14]));
  DiodeForward diodeforward_16 (.in(ADDRESS_out[15]), .out(ADDRESS_in[15]));
  DiodeForward diodeforward_17 (.in(DATA_out[0]), .out(DATA_in[0]));
  DiodeForward diodeforward_18 (.in(DATA_out[1]), .out(DATA_in[1]));
  DiodeForward diodeforward_19 (.in(DATA_out[2]), .out(DATA_in[2]));
  DiodeForward diodeforward_20 (.in(DATA_out[3]), .out(DATA_in[3]));
  DiodeForward diodeforward_21 (.in(DATA_out[4]), .out(DATA_in[4]));
  DiodeForward diodeforward_22 (.in(DATA_out[5]), .out(DATA_in[5]));
  DiodeForward diodeforward_23 (.in(DATA_out[6]), .out(DATA_in[6]));
  DiodeForward diodeforward_24 (.in(DATA_out[7]), .out(DATA_in[7]));
  DiodeForward diodeforward_25 (.in(DATA_out[8]), .out(DATA_in[8]));
  DiodeForward diodeforward_26 (.in(DATA_out[9]), .out(DATA_in[9]));
  DiodeForward diodeforward_27 (.in(DATA_out[10]), .out(DATA_in[10]));
  DiodeForward diodeforward_28 (.in(DATA_out[11]), .out(DATA_in[11]));
  DiodeForward diodeforward_29 (.in(DATA_out[12]), .out(DATA_in[12]));
  DiodeForward diodeforward_30 (.in(DATA_out[13]), .out(DATA_in[13]));
  DiodeForward diodeforward_31 (.in(DATA_out[14]), .out(DATA_in[14]));
  DiodeForward diodeforward_32 (.in(DATA_out[15]), .out(DATA_in[15]));
  Add #(.Bits(16)) OFFSET (.a(REL_out), .b(BASE_out), .c_i(1'b0), .s(OFFSET_s));  // open: c_o
  BarrelShifter #(.Bits(16)) barrelshifter_1 (.in(BASE_out), .shift(5'b00001), .out(barrelshifter_1_out));
  BarrelShifter #(.Bits(16), .direction("right")) barrelshifter_2 (
    .in(BASE_out), .shift(5'b00001), .out(barrelshifter_2_out));
  PullDown pulldown_21 (.out(ADDRESS_in[15]));
  PullDown pulldown_22 (.out(ADDRESS_in[14]));
  PullDown pulldown_23 (.out(ADDRESS_in[13]));
  PullDown pulldown_24 (.out(DATA_in[15]));
  PullDown pulldown_25 (.out(DATA_in[14]));
  PullDown pulldown_26 (.out(DATA_in[13]));
  PullDown pulldown_27 (.out(ADDRESS_in[12]));
  PullDown pulldown_28 (.out(ADDRESS_in[11]));
  PullDown pulldown_29 (.out(ADDRESS_in[10]));
  PullDown pulldown_30 (.out(ADDRESS_in[9]));
  PullDown pulldown_31 (.out(DATA_in[12]));
  PullDown pulldown_32 (.out(DATA_in[11]));
  PullDown pulldown_33 (.out(DATA_in[10]));
  PullDown pulldown_34 (.out(DATA_in[9]));
  PullDown pulldown_35 (.out(ADDRESS_in[7]));
  PullDown pulldown_36 (.out(ADDRESS_in[6]));
  PullDown pulldown_37 (.out(ADDRESS_in[5]));
  PullDown pulldown_38 (.out(ADDRESS_in[8]));
  PullDown pulldown_39 (.out(DATA_in[7]));
  PullDown pulldown_40 (.out(DATA_in[6]));
  PullDown pulldown_41 (.out(DATA_in[5]));
  PullDown pulldown_42 (.out(DATA_in[8]));
  assign ADDRESS_out = ~nOFF_ADSout ? OFFSET_s : 16'bz;  // DriverInvSel driverinvsel_24
  assign DATA_out = ~nOFF_DATout ? OFFSET_s : 16'bz;  // DriverInvSel driverinvsel_25
  assign DATA_out = ~nLSH_DATout ? barrelshifter_1_out : 16'bz;  // DriverInvSel driverinvsel_26
  assign DATA_out = ~nRSH_DATout ? barrelshifter_2_out : 16'bz;  // DriverInvSel driverinvsel_27
  PullDown pulldown_43 (.out(ADDRESS_in[4]));
  PullDown pulldown_44 (.out(ADDRESS_in[3]));
  PullDown pulldown_45 (.out(ADDRESS_in[2]));
  PullDown pulldown_46 (.out(ADDRESS_in[1]));
  PullDown pulldown_47 (.out(DATA_in[4]));
  PullDown pulldown_48 (.out(DATA_in[3]));
  PullDown pulldown_49 (.out(DATA_in[2]));
  PullDown pulldown_50 (.out(DATA_in[1]));
  PullDown #(.Bits(16)) pulldown_51 (.out(ADDRESS_out));
  PullDown #(.Bits(16)) pulldown_52 (.out(DATA_out));
  PullDown #(.Bits(16)) pulldown_53 (.out(DATA_out));
  PullDown #(.Bits(16)) pulldown_54 (.out(DATA_out));
  PullDown pulldown_55 (.out(ADDRESS_in[0]));
  PullDown pulldown_56 (.out(DATA_in[0]));

  // Other names for the same wires on the sheet: CLK_1 = CLK1; CLK_2 = CLK2

  // Notes on the sheet:
  //   Clock: Hz: 10
  //   Control Sequencing
  //   Control Decoding
  //   Memory/IRQ
  //   contents of µCODE (hex, n*v repeats v):
  //   1900000969,1800081c0,100001566,20000a000,0,0,0,0,0,0,0,0,0,0,0,0,3000000000,3000000000,
  //   3000000000,3000000000,3000000000,3000000000,3000000000,3000000000,3000000000,3000000000,
  //   3000000000,3000000000,3000000000,3000000000,3000000000,3000000000,1900000969,1800081c0,
  //   100001566,20000a000,0,0,0,0,0,0,0,0,0,0,0,0,3000000000,3000000000,3000000000,3000000000,
  //   3000000000,3000000000,3000000000,3000000000,3000000000,3000000000,3000000000,3000000000,
  //   3000000000,3000000000,3000000000,3000000000,1900000969,14000012f,10000060e,120000972,
  //   14000a000,1000000cf,10000060e,220001166,0,0,0,0,0,0,0,0,3000000000,3000000000,3000000000,
  //   3000000000,3000000000,3000000000,3000000000,3000000000,3000000000,3000000000,3000000000,
  //   3000000000,3000000000,3000000000,3000000000,3000000000,1900000969,1800081c0,100001566,
  //   20000a000,0,0,0,0,0,0,0,0,0,0,0,0,3000000000,3000000000,3000000000,3000000000,3000000000,
  //   3000000000,3000000000,3000000000,3000000000,3000000000,3000000000,3000000000,3000000000,
  //   3000000000,3000000000,3000000000,1900000969,14000a000,1000000000,0,0,0,0,0,0,0,0,
  //   0,0,0,0,0,3000000000,3000000000,3000000000,3000000000,3000000000,3000000000,3000000000,
  //   3000000000,3000000000,3000000000,3000000000,3000000000,3000000000,3000000000,3000000000,
  //   3000000000,1900000969,1800081c0,100001566,20000a000,0,0,0,0,0,0,0,0,0,0,0,0,3000000000,
  //   3000000000,3000000000,3000000000,3000000000,3000000000,3000000000,3000000000,3000000000,
  //   3000000000,3000000000,3000000000,3000000000,3000000000,3000000000,3000000000,1900000969,
  //   14000012f,10000060e,120000972,14000a000,1000000cf,10000060e,220001166,0,0,0,0,0,0,
  //   0,0,3000000000,3000000000,3000000000,3000000000,3000000000,3000000000,3000000000,
  //   3000000000,3000000000,3000000000,3000000000,3000000000,3000000000,3000000000,3000000000,
  //   3000000000,1900000969,1800081c0,100001566,20000a000,0,0,0,0,0,0,0,0,0,0,0,0,3000000000,
  //   3000000000,3000000000,3000000000,3000000000,3000000000,3000000000,3000000000,3000000000,
  //   3000000000,3000000000,3000000000,3000000000,3000000000,3000000000,3000000000,1900000969,
  //   14000012f,10000060e,120000972,14000a000,1000000cf,10000060e,220001166,0,0,0,0,0,0,
  //   0,0,3000000000,3000000000,3000000000,3000000000,3000000000,3000000000,3000000000,
  //   3000000000,3000000000,3000000000,3000000000,3000000000,3000000000,3000000000,3000000000,
  //   3000000000,1900000969,1800081c0,100001566,20000a000,0,0,0,0,0,0,0,0,0,0,0,0,3000000000,
  //   3000000000,3000000000,3000000000,3000000000,3000000000,3000000000,3000000000,3000000000,
  //   3000000000,3000000000,3000000000,3000000000,3000000000,3000000000,3000000000,1900000969,
  //   14000012f,10000060e,120000972,14000a000,1000000cf,10000060e,220001166,0,0,0,0,0,0,
  //   0,0,3000000000,3000000000,3000000000,3000000000,3000000000,3000000000,3000000000,
  //   3000000000,3000000000,3000000000,3000000000,3000000000,3000000000,3000000000,3000000000,
  //   3000000000,1900000969,1800081c0,100001566,20000a000,0,0,0,0,0,0,0,0,0,0,0,0,3000000000,
  //   3000000000,3000000000,3000000000,3000000000,3000000000,3000000000,3000000000,3000000000,
  //   3000000000,3000000000,3000000000,3000000000,3000000000,3000000000,3000000000,1900000969,
  //   0,0,0,0,0,0,0,0,0,0,0,0,0,0,0,3000000000,3000000000,3000000000,3000000000,3000000000,
  //   3000000000,3000000000,3000000000,3000000000,3000000000,3000000000,3000000000,3000000000,
  //   3000000000,3000000000,3000000000,1900000969,1800081c0,100001566,20000a000,0,0,0,0,
  //   0,0,0,0,0,0,0,0,3000000000,3000000000,3000000000,3000000000,3000000000,3000000000,
  //   3000000000,3000000000,3000000000,3000000000,3000000000,3000000000,3000000000,3000000000,
  //   3000000000,3000000000,1900000969,14000012f,10000060e,120000972,14000a000,1000000cf,
  //   10000060e,220001166,0,0,0,0,0,0,0,0,3000000000,3000000000,3000000000,3000000000,3000000000,
  //   3000000000,3000000000,3000000000,3000000000,3000000000,3000000000,3000000000,3000000000,
  //   3000000000,3000000000,3000000000,1900000969,1800081c0,100001566,20000a000,0,0,0,0,
  //   0,0,0,0,0,0,0,0,3000000000,3000000000,3000000000,3000000000,3000000000,3000000000,
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  //   contents of ROM_16x64k (hex, n*v repeats v):
  //   0,0,0,0,0,0,0,0,0,0,0,0,0,0,0,0,0,0,0,0,0,0,0,0,0,0,0,0,0,0,0,0,0,0,0,0,0,0,0,0,0,
  //   0,0,0,0,0,0,0,0,0,0,0,0,0,0,0,0,0,0,0,0,0,0,0,0,0,0,0,0,0,0,0,0,0,0,0,0,0,0,0,0,0,
  //   0,0,0,0,0,0,0,0,0,0,0,0,0,0,0,0,0,0,0,0,0,0,0,0,0,0,0,0,0,0,0,0,0,0,0,0,0,0,0,0,0,
  //   0,0,0,0,0,0,0,0,0,0,0,0,0,0,0,0,0,0,0,0,0,0,0,0,0,0,0,0,0,0,0,0,0,0,0,0,0,0,0,0,0,
  //   0,0,0,0,0,0,0,0,0,0,0,0,0,0,0,0,0,0,0,0,0,0,0,0,0,0,0,0,0,0,0,0,0,0,0,0,0,0,0,0,0,
  //   0,0,0,0,0,0,0,0,0,0,0,0,0,0,0,0,0,0,0,0,0,0,0,0,0,0,0,0,0,0,0,0,0,0,0,0,0,0,0,0,0,
  //   0,0,0,0,0,0,0,0,0,0,0,0,0,0,0,0,0,0,0,0,0,0,0,0,0,0,0,0,0,0,0,0,0,0,0,0,0,0,0,0,0,
  //   0,0,0,0,0,0,0,0,0,0,0,0,0,0,0,0,0,0,0,0,0,0,0,0,0,0,0,0,0,0,0,0,0,0,0,0,0,0,0,0,0,
  //   0,0,0,0,0,0,0,0,0,0,0,0,0,0,0,0,0,0,0,0,0,0,0,0,0,0,0,0,0,0,0,0,0,0,0,0,0,0,0,0,0,
  //   0,0,0,0,0,0,0,0,0,0,0,0,0,0,0,0,0,0,0,0,0,0,0,0,0,0,0,0,0,0,0,0,0,0,0,0,0,0,0,0,0,
  //   0,0,0,0,0,0,0,0,0,0,0,0,0,0,0,0,0,0,0,0,0,0,0,0,0,0,0,0,0,0,0,0,0,0,0,0,0,0,0,0,0,
  //   0,0,0,0,0,0,0,0,0,0,0,0,0,0,0,0,0,0,0,0,0,0,0,0,0,0,0,0,0,0,0,0,0,0,0,0,0,0,0,0,0,
  //   0,0,0,0,0,0,0,0,0,0,0,0,0,0,0,0,0,0,0,0,0,0,0,0,0,0,0,0,0,0,0,0,0,0,0,0,0,0,0,0,0,
  //   0,0,0,0,0,0,0,0,0,0,0,0,0,0,0,0,0,0,0,0,0,0,0,0,0,0,0,0,0,0,0,0,0,0,0,0,0,0,0,0,0,
  //   0,0,0,0,0,0,0,0,0,0,0,0,0,0,0,0,0,0,0,0,0,0,0,0,0,0,0,0,0,0,0,0,0,0,0,0,0,0,0,0,0,
  //   0,0,0,0,0,0,0,0,0,0,0,0,0,0,0,0,0,0,0,0,0,0,0,0,0,0,0,0,0,0,0,0,0,0,0,0,0,0,0,0,0,
  //   0,0,0,0,0,0,0,0,0,0,0,0,0,0,0,0,0,0,0,0,0,0,0,0,0,0,0,0,0,0,0,0,0,0,0,0,0,0,0,0,0,
  //   0,0,0,0,0,0,0,0,0,0,0,0,0,0,0,0,0,0,0,0,0,0,0,0,0,0,0,0,0,0,0,0,0,0,0,0,0,0,0,0,0,
  //   0,0,0,0,0,0,0,0,0,0,0,0,0,0,0,0,0,0,0,0,0,0,0,0,0,0,0,0,0,0,0,0,0,0,0,0,0,0,0,0,0,
  //   0,0,0,0,0,0,0,0,0,0,0,0,0,0,0,0,0,0,0,0,0,0,0,0,0,0,0,0,0,0,0,0,0,0,0,0,0,0,0,0,0,
  //   0,0,0,0,0,0,0,0,0,0,0,0,0,0,0,0,0,0,0,0,0,0,0,0,0,0,0,0,0,0,0,0,0,0,0,0,0,0,0,0,0,
  //   0,0,0,0,0,0,0,0,0,0,0,0,0,0,0,0,0,0,0,0,0,0,0,0,0,0,0,0,0,0,0,0,0,0,0,0,0,0,0,0,0,
  //   0,0,0,0,0,0,0,0,0,0,0,0,0,0,0,0,0,0,0,0,0,0,0,0,0,0,0,0,0,0,0,0,0,0,0,0,0,0,0,0,0,
  //   0,0,0,0,0,0,0,0,0,0,0,0,0,0,0,0,0,0,0,0,0,0,0,0,0,0,0,0,0,0,0,0,0,0,0,0,0,0,0,0,0,
  //   0,0,0,0,0,0,0,0,0,0,0,0,0,0,0,0,0,0,0,0,0,0,0,0,0,0,0,0,0,0,0,0,0,0,0,0,0,0,0,0,0,
  //   0,0,0,0,0,0,0,0,0,0,0,0,0,0,0,0,0,0,0,0,0,0,0,0,0,0,0,0,0,0,0,0,0,0,0,0,0,0,0,0,0,
  //   0,0,0,0,0,0,0,0,0,0,0,0,0,0,0,0,0,0,0,0,0,0,0,0,0,0,0,0,0,0,0,0,0,0,0,0,0,0,0,0,0,
  //   0,0,0,0,0,0,0,0,0,0,0,0,0,0,0,0,0,0,0,0,0,0,0,0,0,0,0,0,0,0,0,0,0,0,0,0,0,0,0,0,0,
  //   0,0,0,0,0,0,0,0,0,0,0,0,0,0,0,0,0,0,0,0,0,0,0,0,0,0,0,0,0,0,0,0,0,0,0,0,0,0,0,0,0,
  //   0,0,0,0,0,0,0,0,0,0,0,0,0,0,0,0,0,0,0,0,0,0,0,0,0,0,0,0,0,0,0,0,0,0,0,0,0,0,0,0,0,
  //   0,0,0,0,0,0,0,0,0,0,0,0,0,0,0,0,0,0,0,0,0,0,0,0,0,0,0,0,0,0,0,0,0,0,0,0,0,0,0,0,0,
  //   0,0,0,0,0,0,0,0,0,0,0,0,0,0,0,0,0,0,0,0,0,0,0,0,0,0,0,0,0,0,0,0,0,0,0,0,0,0,0,0,0,
  //   0,0,0,0,0,0,0,0,0,0,0,0,0,0,0,0,0,0,0,0,0,0,0,0,0,0,0,0,0,0,0,0,0,0,0,0,0,0,0,0,0,
  //   0,0,0,0,0,0,0,0,0,0,0,0,0,0,0,0,0,0,0,0,0,0,0,0,0,0,0,0,0,0,0,0,0,0,0,0,0,0,0,0,0,
  //   0,0,0,0,0,0,0,0,0,0,0,0,0,0,0,0,0,0,0,0,0,0,0,0,0,0,0,0,0,0,0,0,0,0,0,0,0,0,0,0,0,
  //   0,0,0,0,0,0,0,0,0,0,0,0,0,0,0,0,0,0,0,0,0,0,0,0,0,0,0,0,0,0,0,0,0,0,0,0,0,0,0,0,0,
  //   0,0,0,0,0,0,0,0,0,0,0,0,0,0,0,0,0,0,0,0,0,0,0,0,0,0,0,0,0,0,0,0,0,0,0,0,0,0,0,0,0,
  //   0,0,0,0,0,0,0,0,0,0,0,0,0,0,0,0,0,0,0,0,0,0,0,0,0,0,0,0,0,0,0,0,0,0,0,0,0,0,0,0,0,
  //   0,0,0,0,0,0,0,0,0,0,0,0,0,0,0,0,0,0,0,0,0,0,0,0,0,0,0,0,0,0,0,0,0,0,0,0,0,0,0,0,0,
  //   0,0,0,0,0,0,0,0,0,0,0,0,0,0,0,0,0,0,0,0,0,0,0,0,0,0,0,0,0,0,0,0,0,0,0,0,0,0,0,0,0,
  //   0,0,0,0,0,0,0,0,0,0,0,0,0,0,0,0,0,0,0,0,0,0,0,0,0,0,0,0,0,0,0,0,0,0,0,0,0,0,0,0,0,
  //   0,0,0,0,0,0,0,0,0,0,0,0,0,0,0,0,0,0,0,0,0,0,0,0,0,0,0,0,0,0,0,0,0,0,0,0,0,0,0,0,0,
  //   0,0,0,0,0,0,0,0,0,0,0,0,0,0,0,0,0,0,0,0,0,0,0,0,0,0,0,0,0,0,0,0,0,0,0,0,0,0,0,0,0,
  //   0,0,0,0,0,0,0,0,0,0,0,0,0,0,0,0,0,0,0,0,0,0,0,0,0,0,0,0,0,0,0,0,0,0,0,0,0,0,0,0,0,
  //   0,0,0,0,0,0,0,0,0,0,0,0,0,0,0,0,0,0,0,0,0,0,0,0,0,0,0,0,0,0,0,0,0,0,0,0,0,0,0,0,0,
  //   0,0,0,0,0,0,0,0,0,0,0,0,0,0,0,0,0,0,0,0,0,0,0,0,0,0,0,0,0,0,0,0,0,0,0,0,0,0,0,0,0,
  //   0,0,0,0,0,0,0,0,0,0,0,0,0,0,0,0,0,0,0,0,0,0,0,0,0,0,0,0,0,0,0,0,0,0,0,0,0,0,0,0,0,
  //   0,0,0,0,0,0,0,0,0,0,0,0,0,0,0,0,0,0,0,0,0,0,0,0,0,0,0,0,0,0,0,0,0,0,0,0,0,0,0,0,0,
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  //   ALU
  //   Registers
  //   Control Panel
  //   ATLAS CPU-16
  //   By Hayden B.
endmodule
